# Fritzing sketch Button (saved by Fritzing 0.9.3b)
circuit board: 8.46667cm x 5.64444cm
breadboards: 1

parts:
  S1 = Pushbutton [package="[THT]"]
  U1 = ESP32S-HiLetgo [part_number=ESP32S-HiLetgo]
  R3 = Resistor [tolerance=±5% resistance=220 package=THT]

nets:
  N1: S1.Pin_1, S1.Pin_2, U1.3.3
  N2: S1.Pin_3, S1.Pin_4, U1.GPIO23, R3.Pin_1
  N3: U1.GND, R3.Pin_0

custom parts:
  ESP32S-HiLetgo: HiLetgo ESP-WROOM-32 ESP32 ESP-32S Development Board 2.4GHz Dual-Mode WiFi + Bluetooth Dual Cores Microcontroller The ESP32 integrated with Antenna switches, RF Balun, power amplifiers, low-noise amplifiers, filters, and management modules, and the entire solution occupies the least area of PCB. 2.4 GHz Wi-Fi plus Bluetooth dual-mode chip, with TSMC Ultra-low power consumption 40nm technology,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
